# Fritzing sketch Empfänger (saved by Fritzing 0.9.3b)
circuit board: 2.74955cm x 3.47084cm
breadboards: 1

parts:
  Empfänger = XD-RF-5V - 433Mhz RF receiver [package=THT]
  Tx = female pin header, 1 pin [form="♀ (female)"]
  Ruder = Basic Servo
  Schot = Basic Servo
  StepUp_3_7_zu_5V_(1) = female pin header, 3 pins [form="♀ (female)"]
  StepUp_3_7_zu_5V_(2) = female pin header, 3 pins [form="♀ (female)"]
  R1 = Resistor [tolerance=±5% resistance=10k package=THT]
  J5 = female pin header, 2 pins [form="♀ (female)"]
  J6 = female pin header, 2 pins [form="♀ (female)"]
  U1_(3_7V) = LIPO-110mAh [package=lipo-110]
  S1 = Toggle Switch [package=THT]
  S2 = Toggle Switch [package=THT]
  R5 = Resistor [tolerance=±5% resistance=2.2k package=THT]
  R6 = Resistor [tolerance=±5% resistance=2.2k package=THT]
  U4 = attiny85 [package=dip]
  U2_(3_7V) = LIPO-110mAh [package=lipo-110]
  J7 = female pin header, 3 pins [form="♀ (female)"]
  J8 = female pin header, 1 pin [form="♀ (female)"]
  J9 = female pin header, 2 pins [form="♀ (female)"]

nets:
  N1: Empfänger.VCC, StepUp_3_7_zu_5V_(1).pin3, R1.Pin_0, S2.L1, R5.Pin_0, U4.Pin_8, J7.pin3, J8.pin1
  N2: Empfänger.DATA, U4.Pin_3, J9.pin1
  GND: Empfänger.GND, Ruder.gnd, Schot.gnd, StepUp_3_7_zu_5V_(1).pin2, StepUp_3_7_zu_5V_(2).pin2, J5.pin1, J6.pin1, U1_(3_7V).-, S1.L2, R6.Pin_1, U4.Pin_4, U2_(3_7V).-, J7.pin1, J9.pin2
  N3: Tx.pin1, U4.Pin_7
  VCC: Ruder.vcc, Schot.vcc, StepUp_3_7_zu_5V_(2).pin3
  N4: Ruder.pulse, U4.Pin_6
  N5: Schot.pulse, U4.Pin_5
  N6: StepUp_3_7_zu_5V_(1).pin1, J6.pin2, U1_(3_7V).+
  N7: StepUp_3_7_zu_5V_(2).pin1, J5.pin2, U2_(3_7V).+
  N8: R1.Pin_1, U4.Pin_1
  N9: S1.L1, S2.COM, R5.Pin_1, R6.Pin_0
  N10: S1.COM, U4.Pin_2, J7.pin2

custom parts:
  XD-RF-5V - 433Mhz RF receiver: This is 433Mhz RF transmitter with receiver kit for Arduino ARM MCU wireless Application environment: Remote control switch, receiver module, motorcycles, automobile anti-theft products, home security products, electric doors, shutter doors, windows, remote control socket, remote control LED, remote audio remote control electric doors, garage door remote control, remote control retractable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
