# Fritzing sketch Sender (saved by Fritzing 0.9.3b)
circuit board: 3.78865cm x 2.36071cm
breadboards: 1

parts:
  FS1000A = FS1000A - 433Mhz RF Transmitter [package=THT]
  S1 = Pushbutton [package=THT]
  7805 = Voltage Regulator [package=78xxl]
  Poti_2 = female pin header, 3 pins [form="♀ (female)"]
  Poti_1 = female pin header, 3 pins [form="♀ (female)"]
  Power_in_(z_B_9V) = female pin header, 2 pins [form="♀ (female)"]
  10k = Resistor [tolerance=±5% resistance=10k package=THT]
  220 = Resistor [tolerance=±5% resistance=220 package=THT]
  LED = LED - 5mm [color="Green (570nm)" package="5 mm [THT]"]
  Ruder = Rotary Potentiometer (Small) [maximum_resistance=20kΩ package=THT]
  Schot = Rotary Potentiometer (Small) [maximum_resistance=20kΩ package=THT]
  U4 = attiny85 [package=dip]
  62k = Resistor [tolerance=±5% resistance=62k package=THT]

nets:
  N1: FS1000A.DATA, U4.Pin_5
  N2: FS1000A.VCC, 7805.OUT, Poti_2.pin1, 10k.Pin_1, 220.Pin_1, Schot.leg1, U4.Pin_8, 62k.Pin_0
  GND: FS1000A.GND, 7805.GND, Poti_2.pin3, Poti_1.pin3, Power_in_(z_B_9V).pin1, LED.cathode, Ruder.leg2, Schot.leg2, U4.Pin_4
  N3: S1.leg0, 7805.IN
  N4: S1.leg1, Power_in_(z_B_9V).pin2
  N5: Poti_2.pin2, Schot.wiper, U4.Pin_3
  N6: Poti_1.pin1, Ruder.leg1, 62k.Pin_1
  N7: Poti_1.pin2, Ruder.wiper, U4.Pin_2
  N8: 10k.Pin_0, U4.Pin_1
  N9: 220.Pin_0, LED.anode

custom parts:
  FS1000A - 433Mhz RF Transmitter: This is 433Mhz RF transmitter with receiver kit for Arduino ARM MCU wireless Application environment: Remote control switch, receiver module, motorcycles, automobile anti-theft products, home security products, electric doors, shutter doors, windows, remote control socket, remote control LED, remote audio remote control electric doors, garage door remote control, remote control retractable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

// code stored in the sketch: Tx_01.ino
#include <RCSwitch.h>

RCSwitch mySwitch = RCSwitch();
void setup() {
  mySwitch.enableTransmit(0);  // Sender an D0
}
void loop() {
  mySwitch.send(map(analogRead(A1), 0, 1023, 0, 254), 24); 
  delay(1000);  
}
